// Logisim project add_4.circ as structural Verilog
module add_1 (
  input  A,
  input  B,
  input  vem_1,
  output S,
  output vai_1
);

  wire and_1_out, and_2_out, or_1_out, xor_1_out;

  xor xor_1 (xor_1_out, B, A);
  or or_1 (or_1_out, vem_1, B);
  and and_1 (and_1_out, B, vem_1);
  xor xor_2 (S, vem_1, xor_1_out);
  and and_2 (and_2_out, or_1_out, A);
  or or_2 (vai_1, and_2_out, and_1_out);
endmodule

module add_4 (
  input  [3:0] in_1,
  input  [3:0] in_2,
  output Overflow,
  output [3:0] out_4
);

  wire add_1_2_vai_1, add_1_3_vai_1, add_1_4_vai_1;

  add_1 ADD_1 (.S(out_4[3]), .vai_1(Overflow), .A(in_2[3]), .B(in_1[3]), .vem_1(add_1_3_vai_1));
  add_1 add_1_2 (.S(out_4[1]), .vai_1(add_1_2_vai_1), .A(in_2[1]), .B(in_1[1]), .vem_1(add_1_4_vai_1));
  add_1 add_1_3 (.S(out_4[2]), .vai_1(add_1_3_vai_1), .A(in_2[2]), .B(in_1[2]), .vem_1(add_1_2_vai_1));
  add_1 add_1_4 (.S(out_4[0]), .vai_1(add_1_4_vai_1), .A(in_2[0]), .B(in_1[0]), .vem_1(1'b0));
endmodule

module _8 (
  input  [3:0] in_1,
  input  [3:0] in_2,
  output out_3,
  output [3:0] out_4
);

  // Probe on in_1
  add_4 add_4_1 (.in_2(in_1), .in_1(in_2), .out_4(out_4), .Overflow(out_3));
  // Probe on out_4
  // Probe on in_2
endmodule
