// Logisim project projetos.circ as structural Verilog: 17 circuits, main circuit main
module main (
  input  in_1,
  input  in_2,
  input  [3:0] in_3,
  input  [3:0] in_4,
  input  [3:0] in_5,
  input  in_6,
  input  [3:0] in_7,
  input  [3:0] in_8,
  output out_9,
  output out_10,
  output out_11,
  output [3:0] out_12,
  output [3:0] out_13,
  output [3:0] out_14
);

  add_1 ADD1 (.S(out_11), .vai_1(out_9), .A(in_1), .B(in_2), .vem_1(in_6));
  Sub sub_1 (.A(in_7), .B(in_8), .resultado(out_14));
  add_4 ADD4 (.in_2(in_3), .in_1(in_4), .out_4(out_12), .Overflow(out_10));
  complemento_de_2 complemento_de_2_1 (.in_1(in_5), .out_2(out_13));
endmodule

module add_1 (
  input  A,
  input  B,
  input  vem_1,
  output S,
  output vai_1
);

  wire and_1_out, and_2_out, or_1_out, xor_1_out;

  xor xor_1 (xor_1_out, B, A);
  or or_1 (or_1_out, vem_1, B);
  and and_1 (and_1_out, B, vem_1);
  xor xor_2 (S, vem_1, xor_1_out);
  and and_2 (and_2_out, or_1_out, A);
  or or_2 (vai_1, and_2_out, and_1_out);
endmodule

module add_4 (
  input  [3:0] in_1,
  input  [3:0] in_2,
  output Overflow,
  output [3:0] out_4
);

  wire add_1_2_vai_1, add_1_3_vai_1, add_1_4_vai_1;

  add_1 ADD_1 (.S(out_4[3]), .vai_1(Overflow), .A(in_2[3]), .B(in_1[3]), .vem_1(add_1_2_vai_1));
  add_1 add_1_2 (.S(out_4[2]), .vai_1(add_1_2_vai_1), .A(in_2[2]), .B(in_1[2]), .vem_1(add_1_3_vai_1));
  add_1 add_1_3 (.S(out_4[1]), .vai_1(add_1_3_vai_1), .A(in_2[1]), .B(in_1[1]), .vem_1(add_1_4_vai_1));
  add_1 add_1_4 (.S(out_4[0]), .vai_1(add_1_4_vai_1), .A(in_2[0]), .B(in_1[0]), .vem_1(1'b0));
endmodule

module add_8 (
  input  [3:0] in_1,
  input  [3:0] in_2,
  output out_3,
  output [3:0] out_4
);

  // Probe on in_1
  add_4 add_4_1 (.in_2(in_1), .in_1(in_2), .out_4(out_4), .Overflow(out_3));
  // Probe on out_4
  // Probe on in_2
endmodule

// COMP
module complemento_de_2 (
  input  [3:0] in_1,
  output [3:0] out_2
);

  wire [3:0] not_4_out;

  not not_1 (not_4_out[3], in_1[3]);
  not not_2 (not_4_out[1], in_1[1]);
  not not_3 (not_4_out[2], in_1[2]);
  not not_4 (not_4_out[0], in_1[0]);
  add_4 add_4_1 (.in_2(not_4_out), .in_1(4'b0001), .out_4(out_2));  // open: Overflow
endmodule

// SUB
module Sub (
  input  [3:0] A,
  input  [3:0] B,
  output [3:0] resultado
);

  wire [3:0] complemento_de_2_1_out_2;

  add_4 ADD4 (.in_2(A), .in_1(complemento_de_2_1_out_2), .out_4(resultado));  // open: Overflow
  complemento_de_2 complemento_de_2_1 (.in_1(B), .out_2(complemento_de_2_1_out_2));
endmodule

module converso_a (
  input  D,
  input  C,
  input  B,
  input  A,
  output out_5
);

  wire xnor_1_out;

  xnor xnor_1 (xnor_1_out, B, D);
  or or_1 (out_5, xnor_1_out, A, C);
endmodule

module conversor_b (
  input  B,
  input  C,
  input  D,
  output out_4
);

  wire not_1_out, xnor_1_out;

  not not_1 (not_1_out, B);
  xnor xnor_1 (xnor_1_out, C, D);
  or or_1 (out_4, xnor_1_out, not_1_out);
endmodule

module conversor_c (
  input  B,
  input  C,
  input  D,
  output out_4
);

  wire not_1_out;

  not not_1 (not_1_out, C);
  or or_1 (out_4, D, not_1_out, B);
endmodule

module conversor_d (
  input  A,
  input  B,
  input  C,
  input  D,
  output out_5
);

  wire and_1_out, and_2_out, and_3_out, and_4_out, not_1_out, not_2_out, not_3_out, not_4_out, not_5_out;

  not not_1 (not_1_out, B);
  and and_1 (and_1_out, not_1_out, not_2_out);
  not not_2 (not_2_out, D);
  not not_3 (not_3_out, B);
  and and_2 (and_2_out, not_3_out, C);
  and and_3 (and_3_out, C, not_4_out);
  not not_4 (not_4_out, D);
  and and_4 (and_4_out, B, not_5_out, D);
  not not_5 (not_5_out, C);
  or or_1 (out_5, and_1_out, and_2_out, and_3_out, and_4_out, A);
endmodule

module conversor_e (
  input  B,
  input  C,
  input  D,
  output out_4
);

  wire and_1_out, and_2_out, not_1_out, not_2_out, not_3_out;

  not not_1 (not_1_out, B);
  not not_2 (not_2_out, D);
  not not_3 (not_3_out, D);
  and and_1 (and_1_out, not_1_out, not_2_out);
  and and_2 (and_2_out, C, not_3_out);
  or or_1 (out_4, and_1_out, and_2_out);
endmodule

module conversor_f (
  input  A,
  input  B,
  input  C,
  input  D,
  output out_5
);

  wire and_1_out, and_2_out, and_3_out, not_1_out, not_2_out, not_3_out, not_4_out;

  not not_1 (not_1_out, C);
  not not_2 (not_2_out, D);
  not not_3 (not_3_out, C);
  not not_4 (not_4_out, D);
  and and_1 (and_1_out, not_1_out, not_2_out);
  and and_2 (and_2_out, B, not_3_out);
  and and_3 (and_3_out, B, not_4_out);
  or or_1 (out_5, and_1_out, and_2_out, and_3_out, A);
endmodule

module conversor_g (
  input  A,
  input  B,
  input  C,
  input  D,
  output out_5
);

  wire and_1_out, and_2_out, and_3_out, not_1_out, not_2_out, not_3_out;

  not not_1 (not_1_out, C);
  not not_2 (not_2_out, B);
  not not_3 (not_3_out, D);
  and and_1 (and_1_out, B, not_1_out);
  and and_2 (and_2_out, not_2_out, C);
  and and_3 (and_3_out, C, not_3_out);
  or or_1 (out_5, and_1_out, and_2_out, and_3_out, A);
endmodule

// conversor
module conversor_total (
  input  A,
  input  B,
  input  C,
  input  D,
  output out_5,
  output out_6,
  output out_7,
  output out_8,
  output out_9,
  output out_10,
  output out_11
);

  wire and_1_out, and_2_out, and_3_out, and_4_out, and_5_out, and_6_out, and_7_out, and_8_out, and_9_out,
       and_10_out, and_11_out, and_12_out, not_1_out, not_2_out, not_3_out, not_4_out, not_5_out, not_6_out,
       not_7_out, not_8_out, not_9_out, not_10_out, not_11_out, not_12_out, not_13_out, not_14_out,
       not_15_out, not_16_out, not_17_out, xnor_1_out, xnor_2_out;

  not not_1 (not_1_out, C);
  not not_2 (not_2_out, B);
  not not_3 (not_3_out, D);
  not not_4 (not_4_out, B);
  not not_5 (not_5_out, D);
  not not_6 (not_6_out, C);
  not not_7 (not_7_out, B);
  not not_8 (not_8_out, D);
  not not_9 (not_9_out, D);
  not not_10 (not_10_out, C);
  not not_11 (not_11_out, D);
  not not_12 (not_12_out, C);
  not not_13 (not_13_out, D);
  not not_14 (not_14_out, C);
  not not_15 (not_15_out, B);
  not not_16 (not_16_out, D);
  not not_17 (not_17_out, B);
  and and_1 (and_1_out, not_2_out, not_3_out);
  and and_2 (and_2_out, not_4_out, C);
  and and_3 (and_3_out, C, not_5_out);
  and and_4 (and_4_out, B, not_6_out, D);
  and and_5 (and_5_out, not_7_out, not_8_out);
  and and_6 (and_6_out, C, not_9_out);
  and and_7 (and_7_out, not_10_out, not_11_out);
  and and_8 (and_8_out, B, not_12_out);
  and and_9 (and_9_out, B, not_13_out);
  and and_10 (and_10_out, B, not_14_out);
  and and_11 (and_11_out, not_15_out, C);
  and and_12 (and_12_out, C, not_16_out);
  xnor xnor_1 (xnor_1_out, B, D);
  xnor xnor_2 (xnor_2_out, C, D);
  or or_1 (out_7, D, not_1_out, B);
  or or_2 (out_6, xnor_2_out, not_17_out);
  or or_3 (out_8, and_1_out, and_2_out, and_3_out, and_4_out, A);
  or or_4 (out_9, and_5_out, and_6_out);
  or or_5 (out_11, and_10_out, and_11_out, and_12_out, A);
  or or_6 (out_5, xnor_1_out, A, C);
  or or_7 (out_10, and_7_out, and_8_out, and_9_out, A);
endmodule

module display_7_segmentos (
);

  wire clock_1_out, conversor_total_1_out_5, conversor_total_1_out_6, conversor_total_1_out_7,
       conversor_total_1_out_8, conversor_total_1_out_9, conversor_total_1_out_10, conversor_total_1_out_11;
  wire [3:0] counter_1_q;

  Clock clock_1 (.out(clock_1_out));
  Counter #(.width(4), .max('h9)) counter_1 (.Q(counter_1_q), .clk(clock_1_out));  // open: load, D, count, carry, clr
  conversor_total conversor_total_1 (
    .A(counter_1_q[3]), .B(counter_1_q[2]), .C(counter_1_q[1]), .D(counter_1_q[0]),
    .out_5(conversor_total_1_out_5), .out_6(conversor_total_1_out_6), .out_7(conversor_total_1_out_7),
    .out_8(conversor_total_1_out_8), .out_9(conversor_total_1_out_9), .out_10(conversor_total_1_out_10),
    .out_11(conversor_total_1_out_11));
  _7_Segment_Display u_7_segment_display_1 (
    .g(conversor_total_1_out_11), .f(conversor_total_1_out_10), .a(conversor_total_1_out_5),
    .b(conversor_total_1_out_6), .e(conversor_total_1_out_9), .d(conversor_total_1_out_8),
    .c(conversor_total_1_out_7));  // open: dp
endmodule

module contador (
  output out_1,
  output out_2,
  output out_3,
  output out_4,
  output out_5,
  output out_6,
  output out_7,
  output out_8,
  output out_9
);

  wire clock_1_out, clock_2_out, j_k_ff_5_qn, j_k_ff_6_qn, j_k_ff_7_qn, j_k_ff_8_qn;

  Clock clock_1 (.out(clock_1_out));
  J_K_Flip_Flop j_k_ff_1 (.J(1'b1), .clk(clock_1_out), .K(1'b1), .Q(out_4));  // open: Qn, preset, en, reset
  // Probe on {out_1, out_2, out_3, out_4}
  J_K_Flip_Flop j_k_ff_2 (.J(1'b1), .clk(out_4), .K(1'b1), .Q(out_3));  // open: Qn, preset, en, reset
  J_K_Flip_Flop j_k_ff_3 (.J(1'b1), .clk(out_3), .K(1'b1), .Q(out_2));  // open: Qn, preset, en, reset
  J_K_Flip_Flop j_k_ff_4 (.J(1'b1), .clk(out_2), .K(1'b1), .Q(out_1));  // open: Qn, preset, en, reset
  J_K_Flip_Flop j_k_ff_5 (
    .J(1'b1), .clk(clock_2_out), .K(1'b1), .Q(out_9), .Qn(j_k_ff_5_qn));  // open: preset, en, reset
  Clock clock_2 (.out(clock_2_out));
  J_K_Flip_Flop j_k_ff_6 (
    .J(1'b1), .clk(j_k_ff_5_qn), .K(1'b1), .Q(out_8), .Qn(j_k_ff_6_qn));  // open: preset, en, reset
  J_K_Flip_Flop j_k_ff_7 (
    .J(1'b1), .clk(j_k_ff_6_qn), .K(1'b1), .Q(out_7), .Qn(j_k_ff_7_qn));  // open: preset, en, reset
  // Probe on {out_5, out_6, out_7, out_8, out_9}
  J_K_Flip_Flop j_k_ff_8 (
    .J(1'b1), .clk(j_k_ff_7_qn), .K(1'b1), .Q(out_6), .Qn(j_k_ff_8_qn));  // open: preset, en, reset
  J_K_Flip_Flop j_k_ff_9 (.J(1'b1), .clk(j_k_ff_8_qn), .K(1'b1), .Q(out_5));  // open: Qn, preset, en, reset

  // Notes on the sheet:
  //   ASSINCRONO DOWN
  //   ASSINCRONO UP
endmodule

module contador_sincrono (
  output out_1,
  output out_2,
  output out_3
);

  wire clock_1_out, j_k_ff_1_qn, j_k_ff_2_qn;

  Clock clock_1 (.out(clock_1_out));
  J_K_Flip_Flop j_k_ff_1 (
    .J(out_2), .clk(clock_1_out), .K(j_k_ff_2_qn), .Q(out_1), .Qn(j_k_ff_1_qn));  // open: preset, en, reset
  // Probe on {out_1, out_2, out_3}
  J_K_Flip_Flop j_k_ff_2 (
    .J(j_k_ff_1_qn), .clk(clock_1_out), .K(out_1), .Q(out_2), .Qn(j_k_ff_2_qn));  // open: preset, en, reset
  J_K_Flip_Flop j_k_ff_3 (.J(1'b1), .clk(clock_1_out), .K(j_k_ff_2_qn), .Q(out_3));  // open: Qn, preset, en, reset
endmodule
